// Digital circuit 1_Mux_8entradas.dig as structural Verilog
module _1_Mux_8entradas (
  input  D0,
  input  Sel1,
  input  D1,
  input  D3,
  input  D2,
  input  Sel0,
  input  D4,
  input  D5,
  input  D6,
  input  D7,
  input  Sel2,
  output Output
);

  wire and_1_out, and_2_out, and_3_out, and_4_out, and_5_out, and_6_out, and_7_out, and_8_out, not_1_out,
       not_2_out, not_3_out, or_1_out, or_2_out;

  not not_1 (not_1_out, Sel2);
  not not_2 (not_2_out, Sel1);
  not not_3 (not_3_out, Sel0);
  and and_1 (and_1_out, D7, Sel2, Sel1, Sel0);
  and and_2 (and_2_out, D6, Sel2, Sel1, not_3_out);
  and and_3 (and_3_out, D5, Sel2, not_2_out, Sel0);
  and and_4 (and_4_out, D4, Sel2, not_2_out, not_3_out);
  and and_5 (and_5_out, D3, not_1_out, Sel1, Sel0);
  and and_6 (and_6_out, D2, not_1_out, Sel1, not_3_out);
  and and_7 (and_7_out, D1, not_1_out, not_2_out, Sel0);
  and and_8 (and_8_out, D0, not_1_out, not_2_out, not_3_out);
  or or_1 (or_1_out, and_1_out, and_2_out, and_3_out, and_4_out);
  or or_2 (or_2_out, and_5_out, and_6_out, and_7_out, and_8_out);
  or or_3 (Output, or_1_out, or_2_out);

  // Notes on the sheet:
  //   La entrada activa se define por el número en binario
  //   Sel2-Sel1-Sel0. 
  //   Ejm: 101 la entrada activa es D5
endmodule
