// Digital circuit 2_Demux_4salidas.dig as structural Verilog
module _2_Demux_4salidas (
  input  Input,
  input  Sel0,
  input  Sel1,
  output Out3,
  output Out2,
  output Out1,
  output Out0
);

  wire not_1_out, not_2_out;

  not not_1 (not_1_out, Sel1);
  not not_2 (not_2_out, Sel0);
  and and_1 (Out3, Input, Sel1, Sel0);
  and and_2 (Out2, Input, Sel1, not_2_out);
  and and_3 (Out1, Input, not_1_out, Sel0);
  and and_4 (Out0, Input, not_1_out, not_2_out);

  // Notes on the sheet:
  //   La salida activa se define por el número en binario
  //   Sel1-Sel0. 
  //   Ejm: 10 la salida activa es Out2
endmodule
