// Digital circuit 3a_RS-FilpFlop.dig as structural Verilog
module _3a_RS_FilpFlop (
  input  R,
  input  C,
  input  S,
  output Q
);

  wire and_1_out, and_2_out, and_3_out, and_4_out, nor_1_out, nor_2_out, nor_4_out, not_1_out;

  and and_1 (and_1_out, S, C);
  not not_1 (not_1_out, C);
  and and_2 (and_2_out, C, R);
  nor nor_1 (nor_1_out, and_1_out, nor_2_out);
  nor nor_2 (nor_2_out, nor_1_out, and_2_out);
  and and_3 (and_3_out, nor_1_out, not_1_out);
  and and_4 (and_4_out, not_1_out, nor_2_out);
  nor nor_3 (Q, and_3_out, nor_4_out);
  nor nor_4 (nor_4_out, Q, and_4_out);

  // Notes on the sheet:
  //   R: Set input
  //   {{de Set Eingang}}
  //   C: gate input
  //   {{de Freigabeeingang}}
  //   S: Reset input
  //   {{de Reset Eingang}}
  //   Q: The stored bit.
  //   {{de Das gespeicherte Bit}}
  //   Maestro-esclavo es una combinación de dos latchs conectados
  //   en serie, donde uno actúa como maestro y otro como esclavo
  //   Cada flip-flop está conectado a un pulso de reloj complementario entre sí
  //   Sólo cuando la señal de reloj cambia de 1 a 0 puede la salida 
  //   afectarse de acuerdo con los valores de la entrada S y R
  //   Si tanto S como R son 0 durante la transición 
  //   de reloj, la salida no cambia
  //   Cuando tanto S como R son iguales a 1, la salida es impredecible
  //   y puede ser 0 o 1 dependiendo de los retrasos internos de
  //   tiempo que ocurran dentro del circuito.
  //   Master
  //   Slave
endmodule
