// Digital circuit 3b_JK-FlipFlop.dig as structural Verilog
module _3b_JK_FlipFlop (
  input  J,
  input  K,
  input  C,
  output Q
);

  wire and_1_out, and_2_out, and_3_out, and_4_out, and_5_out, and_6_out, nor_1_out, nor_2_out, nor_3_out,
       not_1_out;

  and and_1 (and_1_out, nor_3_out, J);
  and and_2 (and_2_out, K, Q);
  and and_3 (and_3_out, and_1_out, C);
  not not_1 (not_1_out, C);
  and and_4 (and_4_out, C, and_2_out);
  nor nor_1 (nor_1_out, and_3_out, nor_2_out);
  nor nor_2 (nor_2_out, nor_1_out, and_4_out);
  and and_5 (and_5_out, nor_2_out, not_1_out);
  and and_6 (and_6_out, not_1_out, nor_1_out);
  nor nor_3 (nor_3_out, and_5_out, Q);
  nor nor_4 (Q, nor_3_out, and_6_out);

  // Notes on the sheet:
  //   Q: The stored bit.
  //   {{de Das gespeicherte Bit}}
  //   El funcionamiento del flip-flop JK es similar al flip-flop SR, pero  
  //   cuando J = 1 y K = 1, flip flop alterna, eso significa
  //   que el estado de salida cambia  de su estado anterior.
  //   La entrada J es la equivalente a la entrada S de un flip-flop R-S y 
  //   la entrada K, al equivalente a la entrada R
  //   Master
  //   Slave
endmodule
